// Logisim project logisism.circ as structural Verilog: 1 circuit, main circuit main
module main (
  input  in_1,
  input  in_2,
  input  in_3,
  input  in_4,
  input  in_5,
  input  in_6,
  input  in_7,
  input  B_prime,
  input  C_prime,
  input  in_10,
  input  D_prime,
  input  A_prime,
  input  D,
  output out_14,
  output out_15,
  output F_prime
);

  wire and_2_out, or_1_out, or_2_out, or_3_out, xor_1_out;

  xor xor_1 (xor_1_out, in_2, in_5);
  or or_1 (or_1_out, B_prime, C_prime);
  or or_2 (or_2_out, B_prime, D_prime);
  or or_3 (or_3_out, A_prime, D);
  and and_1 (F_prime, or_1_out, or_2_out, or_3_out);
  buf and_2 (and_2_out, in_1);  // AND_Gate
  // NOT_Gate not_1 has open pins: in=and_2_out, out=open
  or or_4 (out_15, in_7, in_10);
  and and_3 (out_14, in_4, in_6, in_6, in_6, in_6);
endmodule
